# Fritzing sketch fritzing cercuit (saved by Fritzing 0.9.3b)
breadboards: 1

parts:
  ESP32_-_Back1 = ESP32 - CAM
  Part1 = RDM6300-ANT
  125_kHz_RFID_module2 = RDM6300
  OLED_I2C1 = OLED 128x64 I2C Monochrome Display
  LED2 = LEDs [package=led-1206]

nets:
  N1: ESP32_-_Back1.GPIO2, LED2.A
  N2: ESP32_-_Back1.GPIO14, OLED_I2C1.SCK
  N3: ESP32_-_Back1.GPIO15, OLED_I2C1.SDA
  N4: ESP32_-_Back1.GPIO13, 125_kHz_RFID_module2.TX, 125_kHz_RFID_module2.GND#66, 125_kHz_RFID_module2.GND#67
  N5: ESP32_-_Back1.GND#7, 125_kHz_RFID_module2.GND#60, OLED_I2C1.GND, LED2.C
  5V: ESP32_-_Back1.5V, 125_kHz_RFID_module2.+5V#61, OLED_I2C1.VDD
  N6: Part1.ANT1, 125_kHz_RFID_module2.ANT1
  N7: Part1.ANT2, 125_kHz_RFID_module2.ANT2

custom parts:
  ESP32 - CAM: The ESP32-CAM has a very competitive small-size camera module that can operate independently as a minimum system with a footprint of only 27*40.5*4.5mm and a deep sleep current of up to 6mA.
  RDM6300-ANT: Antenna
  RDM6300: 125 kHz RFID module (serial interface)
